// Logisim project Main ALU.circ as structural Verilog: 17 circuits, main circuit ALU
module main (
  input  E
);

  wire alu_1_over, alu_1_zero, clock_1_out, d_ff_1_q, d_ff_2_q, not_1_out, not_2_out, Reset_out, rgb_1_e_3,
       uc_1_clk_ac, uc_1_clk_pc, uc_1_clk_ram, uc_1_clk_ri, uc_1_d, uc_1_e, uc_1_load, uc_1_r_w, uc_1_rst_pc;
  wire [2:0] uc_1_s;
  wire [3:0] alu_1_s, mux_1_s, PC_q, ram_1_data, registrador_ac_1_q, uc_1_dados, \uc_1_endereçamento ,
       uc_1_operando;
  wire [7:0] registrador_ir_1_q, rom_1_data;

  RGB rgb_1 (.E(E), .E_3(rgb_1_e_3));  // open: E_2
  Counter #(.width(4), .max('hf), .trigger("falling")) PC (
    .load(uc_1_load), .D(uc_1_dados), .count(not_1_out), .Q(PC_q), .clk(uc_1_clk_pc), .clr(uc_1_rst_pc));  // open: carry
  not not_1 (not_1_out, uc_1_load);
  // Probe on rom_1_data
  ROM #(.addrWidth(4)) rom_1 (.addr(PC_q), .data(rom_1_data));  // open: sel
  Registrador_IR registrador_ir_1 (.Q(registrador_ir_1_q), .D(rom_1_data), .Clock(uc_1_clk_ri));
  UC uc_1 (
    .Operando(uc_1_operando), .D(uc_1_d), .E(uc_1_e), .S(uc_1_s), .\Instrução (registrador_ir_1_q),
    .\Endereçamento (\uc_1_endereçamento ), .Clock(clock_1_out), .Reset(Reset_out), .Rst_PC(uc_1_rst_pc),
    .clk_RI(uc_1_clk_ri), .clk_PC(uc_1_clk_pc), .clk_AC(uc_1_clk_ac), .clk_RAM(uc_1_clk_ram),
    .Zero(d_ff_2_q), .Load(uc_1_load), .Overflow(d_ff_1_q), .Dados(uc_1_dados), .R_W(uc_1_r_w));
  Button Reset (.out(Reset_out));
  Clock clock_1 (.out(clock_1_out));
  MUX mux_1 (.E(uc_1_operando), .Controle(uc_1_e), .D(ram_1_data), .S(mux_1_s));
  ALU alu_1 (
    .A(registrador_ac_1_q), .B(mux_1_s), .CMD(uc_1_s), .S(alu_1_s), .D(uc_1_d), .Over(alu_1_over),
    .Zero(alu_1_zero));
  // Probe on alu_1_s
  // Probe on registrador_ac_1_q
  Registrador_AC registrador_ac_1 (.Q(registrador_ac_1_q), .D(alu_1_s), .Clock(uc_1_clk_ac));
  RAM #(.addrWidth(4), .dataWidth(4)) ram_1 (
    .addr(\uc_1_endereçamento ), .data(ram_1_data), .clk(uc_1_clk_ram), .ld(uc_1_r_w));  // open: sel, clr
  not not_2 (not_2_out, uc_1_r_w);
  // Probe on mux_1_s
  D_Flip_Flop d_ff_1 (.clk(uc_1_clk_ac), .D(alu_1_over), .Q(d_ff_1_q));  // open: Qn, preset, en, reset
  D_Flip_Flop d_ff_2 (.clk(uc_1_clk_ac), .D(alu_1_zero), .Q(d_ff_2_q));  // open: Qn, preset, en, reset
  Buffer buffer_1 (.A(registrador_ac_1_q), .A_2(not_2_out), .S(ram_1_data));

  // Notes on the sheet:
  //   0
  //   1
  //   2
  //   3
  //   4
  //   5
  //   6
  //   7
  //   8
  //   9
  //   A
  //   B
  //   C
  //   D
  //   E
  //   F
  //   Instruction Set
  //   0
  //   000
  //   MOV
  //   1
  //   000
  //   MOV
  //   0
  //   001
  //   ADD
  //   1
  //   001
  //   ADD
  //   SUB
  //   010
  //   0
  //   1
  //   010
  //   SUB
  //   0
  //   OR
  //   011
  //   1
  //   OR
  //   011
  //   0
  //   NOT
  //   100
  //   100
  //   NOT
  //   1
  //   0
  //   101
  //   SHF
  //   1
  //   101
  //   SHF
  //   0
  //   110
  //   JPZ
  //   JPO
  //   1
  //   110
  //   111
  //   0
  //   GO
  //   STR
  //   1
  //   111
  //   AC <= X
  //   AC <= M(X)
  //   AC <= AC+X
  //   AC <= AC+M(X)
  //   AC <= AC-X
  //   AC <= AC-M(X)
  //   AC <= AC OR X
  //   AC <= AC OR M(X)
  //   AC <= NOT X
  //   AC <= NOT M( X)
  //   AC <= AC << Q
  //   AC <= AC >> Q
  //   PC <= X SE FLAG Z
  //   PC <= X SE FLAG O
  //   PC <= X
  //   M(X) <= AC 
  //   contents of rom_1 (hex, n*v repeats v):
  //   0 f0 1 f1 10 31 d0 f2 11 f0 12 f1 e4
endmodule

module ALU (
  input  D,
  input  [3:0] A,
  input  [3:0] B,
  input  [2:0] CMD,
  output Over,
  output Zero,
  output [3:0] S
);

  wire and_1_out, and_2_out, decoder_3x8_1_s0, decoder_3x8_1_s1, decoder_3x8_1_s2, decoder_3x8_1_s3,
       decoder_3x8_1_s4, decoder_3x8_1_s5, decoder_3x8_1_s6, decoder_3x8_1_s7, not_1_out, soma_4_1_out_3,
       sub_4_1_vai_1;
  wire [3:0] buffer_5_s, or_4_1_s, rot_d_1_abcd_2, rot_e_1_abcd_2, soma_4_1_out_4, sub_4_1_out_4;

  or or_1 (Over, and_1_out, and_2_out);
  and and_1 (and_1_out, soma_4_1_out_3, decoder_3x8_1_s1);
  and and_2 (and_2_out, sub_4_1_vai_1, decoder_3x8_1_s2);
  Decoder_3x8 decoder_3x8_1 (
    .S0(decoder_3x8_1_s0), .S1(decoder_3x8_1_s1), .S2(decoder_3x8_1_s2), .S3(decoder_3x8_1_s3),
    .S4(decoder_3x8_1_s4), .S5(decoder_3x8_1_s5), .S6(decoder_3x8_1_s6), .S7(decoder_3x8_1_s7), .CMD(CMD));
  nor nor_1 (Zero, decoder_3x8_1_s7, decoder_3x8_1_s6, S[0], S[1], S[2], S[3]);
  Buffer buffer_1 (.A(B), .A_2(decoder_3x8_1_s0), .S(S));
  Soma_4 soma_4_1 (.A(A), .out_3(soma_4_1_out_3), .B(B), .out_4(soma_4_1_out_4));
  Buffer buffer_2 (.A(soma_4_1_out_4), .A_2(decoder_3x8_1_s1), .S(S));
  Sub_4 sub_4_1 (.A(A), .Vai_1(sub_4_1_vai_1), .in_2(B), .out_4(sub_4_1_out_4));
  Buffer buffer_3 (.A(sub_4_1_out_4), .A_2(decoder_3x8_1_s2), .S(S));
  Or_4 or_4_1 (.A(A), .B(B), .S(or_4_1_s));
  Buffer buffer_4 (.A(or_4_1_s), .A_2(decoder_3x8_1_s3), .S(S));
  Buffer_Inversor buffer_inversor_1 (.A(B), .A_2(decoder_3x8_1_s4), .S(S));
  Rot_D rot_d_1 (.abcd_2(rot_d_1_abcd_2), .ABCD(A), .XY(B[1:0]));
  Rot_E rot_e_1 (.abcd_2(rot_e_1_abcd_2), .ABCD(A), .XY(B[1:0]));
  not not_1 (not_1_out, D);
  Buffer buffer_5 (.A(rot_d_1_abcd_2), .A_2(D), .S(buffer_5_s));
  Buffer buffer_6 (.A(rot_e_1_abcd_2), .A_2(not_1_out), .S(buffer_5_s));
  Buffer buffer_7 (.A(buffer_5_s), .A_2(decoder_3x8_1_s5), .S(S));
endmodule

module Buffer (
  input  [3:0] A,
  input  A_2,
  output [3:0] S
);

  assign S[2] = A_2 ? A[2] : 1'bz;  // Controlled_Buffer controlled_buffer_1
  assign S[1] = A_2 ? A[1] : 1'bz;  // Controlled_Buffer controlled_buffer_2
  assign S[3] = A_2 ? A[3] : 1'bz;  // Controlled_Buffer controlled_buffer_3
  assign S[0] = A_2 ? A[0] : 1'bz;  // Controlled_Buffer controlled_buffer_4
endmodule

module Buffer_Inversor (
  input  [3:0] A,
  input  A_2,
  output [3:0] S
);

  assign S[1] = A_2 ? ~A[1] : 1'bz;  // Controlled_Inverter controlled_inverter_1
  assign S[2] = A_2 ? ~A[2] : 1'bz;  // Controlled_Inverter controlled_inverter_2
  assign S[3] = A_2 ? ~A[3] : 1'bz;  // Controlled_Inverter controlled_inverter_3
  assign S[0] = A_2 ? ~A[0] : 1'bz;  // Controlled_Inverter controlled_inverter_4
endmodule

module Decoder_3x8 (
  input  [2:0] CMD,
  output S0,
  output S1,
  output S2,
  output S3,
  output S4,
  output S5,
  output S6,
  output S7
);

  wire not_1_out, not_2_out, not_3_out, not_4_out, not_5_out, not_6_out, not_7_out, not_8_out, not_9_out,
       not_10_out, not_11_out, not_12_out;

  not not_1 (not_1_out, CMD[2]);
  and and_1 (S0, not_1_out, not_2_out, not_3_out);
  not not_2 (not_2_out, CMD[1]);
  not not_3 (not_3_out, CMD[0]);
  not not_4 (not_4_out, CMD[2]);
  and and_2 (S1, not_4_out, not_5_out, CMD[0]);
  not not_5 (not_5_out, CMD[1]);
  not not_6 (not_6_out, CMD[2]);
  and and_3 (S2, not_6_out, CMD[1], not_7_out);
  not not_7 (not_7_out, CMD[0]);
  not not_8 (not_8_out, CMD[2]);
  and and_4 (S3, not_8_out, CMD[1], CMD[0]);
  not not_9 (not_9_out, CMD[1]);
  and and_5 (S4, CMD[2], not_9_out, not_10_out);
  not not_10 (not_10_out, CMD[0]);
  not not_11 (not_11_out, CMD[1]);
  and and_6 (S5, CMD[2], not_11_out, CMD[0]);
  and and_7 (S6, CMD[2], CMD[1], not_12_out);
  not not_12 (not_12_out, CMD[0]);
  and and_8 (S7, CMD[2], CMD[1], CMD[0]);
endmodule

module Or_4 (
  input  [3:0] A,
  input  [3:0] B,
  output [3:0] S
);

  or or_1 (S[3], A[3], B[3]);
  or or_2 (S[2], A[2], B[2]);
  or or_3 (S[1], A[1], B[1]);
  or or_4 (S[0], A[0], B[0]);
endmodule

module Rot_D (
  input  [3:0] ABCD,
  input  [1:0] XY,
  output [3:0] abcd_2
);

  wire and_1_out, and_2_out, and_3_out, and_4_out, and_5_out, and_6_out, and_7_out, and_8_out, and_9_out;

  and and_1 (and_1_out, ~XY[1], ~XY[0], ABCD[0]);  // AND_Gate
  and and_2 (and_2_out, ~XY[1], XY[0], ABCD[1]);  // AND_Gate
  and and_3 (and_3_out, XY[1], ~XY[0], ABCD[2]);  // AND_Gate
  and and_4 (and_4_out, XY[1], XY[0], ABCD[3]);
  and and_5 (and_5_out, ~XY[1], ~XY[0], ABCD[1]);  // AND_Gate
  and and_6 (and_6_out, ~XY[1], XY[0], ABCD[2]);  // AND_Gate
  and and_7 (and_7_out, XY[1], ~XY[0], ABCD[3]);  // AND_Gate
  and and_8 (and_8_out, ~XY[1], ~XY[0], ABCD[2]);  // AND_Gate
  and and_9 (and_9_out, ~XY[1], XY[0], ABCD[3]);  // AND_Gate
  and and_10 (abcd_2[3], ~XY[1], ~XY[0], ABCD[3]);  // AND_Gate
  or or_1 (abcd_2[0], and_1_out, and_2_out, and_3_out, and_4_out);
  or or_2 (abcd_2[1], and_5_out, and_6_out, and_7_out);
  or or_3 (abcd_2[2], and_8_out, and_9_out);
endmodule

module Rot_E (
  input  [3:0] ABCD,
  input  [1:0] XY,
  output [3:0] abcd_2
);

  wire and_1_out, and_2_out, and_3_out, and_4_out, and_5_out, and_6_out, and_7_out, and_8_out, and_9_out;

  and and_1 (and_1_out, ~XY[1], ~XY[0], ABCD[0]);  // AND_Gate
  and and_2 (and_2_out, ~XY[1], XY[0], ABCD[1]);  // AND_Gate
  and and_3 (and_3_out, XY[1], ~XY[0], ABCD[2]);  // AND_Gate
  and and_4 (and_4_out, XY[1], XY[0], ABCD[3]);
  and and_5 (and_5_out, ~XY[1], ~XY[0], ABCD[1]);  // AND_Gate
  and and_6 (and_6_out, ~XY[1], XY[0], ABCD[2]);  // AND_Gate
  and and_7 (and_7_out, XY[1], ~XY[0], ABCD[3]);  // AND_Gate
  and and_8 (and_8_out, ~XY[1], ~XY[0], ABCD[2]);  // AND_Gate
  and and_9 (and_9_out, ~XY[1], XY[0], ABCD[3]);  // AND_Gate
  and and_10 (abcd_2[0], ~XY[1], ~XY[0], ABCD[3]);  // AND_Gate
  or or_1 (abcd_2[3], and_1_out, and_2_out, and_3_out, and_4_out);
  or or_2 (abcd_2[2], and_5_out, and_6_out, and_7_out);
  or or_3 (abcd_2[1], and_8_out, and_9_out);
endmodule

module Sub_1 (
  input  A,
  input  B,
  input  Vem_1,
  output Sub,
  output Vai_1
);

  wire and_1_out, and_2_out, not_1_out, or_1_out, xor_1_out;

  not not_1 (not_1_out, A);
  or or_1 (or_1_out, B, Vem_1);
  xor xor_1 (xor_1_out, A, B);
  xor xor_2 (Sub, xor_1_out, Vem_1);
  and and_1 (and_1_out, or_1_out, not_1_out);
  and and_2 (and_2_out, B, Vem_1);
  or or_2 (Vai_1, and_1_out, and_2_out);
endmodule

module Sub_4 (
  input  [3:0] A,
  input  [3:0] in_2,
  output Vai_1,
  output [3:0] out_4
);

  wire sub_1_2_vai_1, sub_1_3_vai_1, sub_1_4_vai_1;

  Sub_1 sub_1_1 (.A(A[3]), .B(in_2[3]), .Vem_1(sub_1_2_vai_1), .Sub(out_4[3]), .Vai_1(Vai_1));
  Sub_1 sub_1_2 (.A(A[2]), .B(in_2[2]), .Vem_1(sub_1_3_vai_1), .Sub(out_4[2]), .Vai_1(sub_1_2_vai_1));
  Sub_1 sub_1_3 (.A(A[1]), .B(in_2[1]), .Vem_1(sub_1_4_vai_1), .Sub(out_4[1]), .Vai_1(sub_1_3_vai_1));
  Sub_1 sub_1_4 (.A(A[0]), .B(in_2[0]), .Vem_1(1'b0), .Sub(out_4[0]), .Vai_1(sub_1_4_vai_1));
endmodule

module Soma_1 (
  input  A,
  input  B,
  input  Vem_1,
  output Soma,
  output Vai_1
);

  wire and_1_out, and_2_out, or_1_out, xor_1_out;

  or or_1 (or_1_out, B, Vem_1);
  xor xor_1 (xor_1_out, A, B);
  xor xor_2 (Soma, xor_1_out, Vem_1);
  and and_1 (and_1_out, or_1_out, A);
  and and_2 (and_2_out, B, Vem_1);
  or or_2 (Vai_1, and_1_out, and_2_out);
endmodule

module Soma_4 (
  input  [3:0] B,
  input  [3:0] A,
  output out_3,
  output [3:0] out_4
);

  wire soma_1_2_vai_1, soma_1_3_vai_1, soma_1_4_vai_1;

  Soma_1 soma_1_1 (.A(A[3]), .B(B[3]), .Vem_1(soma_1_2_vai_1), .Soma(out_4[3]), .Vai_1(out_3));
  Soma_1 soma_1_2 (.A(A[2]), .B(B[2]), .Vem_1(soma_1_3_vai_1), .Soma(out_4[2]), .Vai_1(soma_1_2_vai_1));
  Soma_1 soma_1_3 (.A(A[1]), .B(B[1]), .Vem_1(soma_1_4_vai_1), .Soma(out_4[1]), .Vai_1(soma_1_3_vai_1));
  Soma_1 soma_1_4 (.A(A[0]), .B(B[0]), .Vem_1(1'b0), .Soma(out_4[0]), .Vai_1(soma_1_4_vai_1));
endmodule

module Registrador_AC (
  input  Clock,
  input  [3:0] D,
  output [3:0] Q
);

  D_Flip_Flop d_ff_1 (.clk(Clock), .D(D[3]), .Q(Q[3]));  // open: Qn, preset, en, reset
  D_Flip_Flop d_ff_2 (.clk(Clock), .D(D[2]), .Q(Q[2]));  // open: Qn, preset, en, reset
  D_Flip_Flop d_ff_3 (.clk(Clock), .D(D[1]), .Q(Q[1]));  // open: Qn, preset, en, reset
  D_Flip_Flop d_ff_4 (.clk(Clock), .D(D[0]), .Q(Q[0]));  // open: Qn, preset, en, reset
endmodule

module Registrador_IR (
  input  Clock,
  input  [7:0] D,
  output [7:0] Q
);

  D_Flip_Flop #(.trigger("falling")) d_ff_1 (.clk(Clock), .D(D[7]), .Q(Q[7]));  // open: Qn, preset, en, reset
  D_Flip_Flop #(.trigger("falling")) d_ff_2 (.clk(Clock), .D(D[6]), .Q(Q[6]));  // open: Qn, preset, en, reset
  D_Flip_Flop #(.trigger("falling")) d_ff_3 (.clk(Clock), .D(D[5]), .Q(Q[5]));  // open: Qn, preset, en, reset
  D_Flip_Flop #(.trigger("falling")) d_ff_4 (.clk(Clock), .D(D[4]), .Q(Q[4]));  // open: Qn, preset, en, reset
  D_Flip_Flop #(.trigger("falling")) d_ff_5 (.clk(Clock), .D(D[3]), .Q(Q[3]));  // open: Qn, preset, en, reset
  D_Flip_Flop #(.trigger("falling")) d_ff_6 (.clk(Clock), .D(D[2]), .Q(Q[2]));  // open: Qn, preset, en, reset
  D_Flip_Flop #(.trigger("falling")) d_ff_7 (.clk(Clock), .D(D[1]), .Q(Q[1]));  // open: Qn, preset, en, reset
  D_Flip_Flop #(.trigger("falling")) d_ff_8 (.clk(Clock), .D(D[0]), .Q(Q[0]));  // open: Qn, preset, en, reset
endmodule

module MUX (
  input  [3:0] E,
  input  [3:0] D,
  input  Controle,
  output [3:0] S
);

  wire not_1_out;

  not not_1 (not_1_out, Controle);
  Buffer buffer_1 (.A(E), .A_2(not_1_out), .S(S));
  Buffer buffer_2 (.A(D), .A_2(Controle), .S(S));
endmodule

module UC (
  input  [7:0] \Instrução ,
  input  Clock,
  input  Reset,
  input  Overflow,
  input  Zero,
  output [3:0] Dados,
  output [3:0] \Endereçamento ,
  output [3:0] Operando,
  output Rst_PC,
  output clk_RI,
  output clk_PC,
  output clk_AC,
  output clk_RAM,
  output D,
  output E,
  output [2:0] S,
  output R_W,
  output Load
);

  wire GoTo_out, JPO_out, JPZ_out, nand_2_out;
  wire [1:0] counter_1_q;

  nand nand_1 (R_W, \Instrução [7], \Instrução [6], \Instrução [5], \Instrução [4], clk_AC);
  Counter #(.width(2), .max('h3)) counter_1 (.Q(counter_1_q), .clk(Clock), .clr(Reset));  // open: load, D, count, carry
  and GoTo (GoTo_out, \Instrução [7], \Instrução [6], \Instrução [5], ~\Instrução [4], clk_PC);  // AND_Gate
  and and_1 (clk_RI, ~counter_1_q[0], ~counter_1_q[1]);  // AND_Gate
  and JPO (JPO_out, \Instrução [7], \Instrução [6], ~\Instrução [5], \Instrução [4], clk_PC, Overflow);  // AND_Gate
  or or_1 (Load, GoTo_out, JPO_out, JPZ_out);
  and and_2 (clk_PC, counter_1_q[0], ~counter_1_q[1]);  // AND_Gate
  and and_3 (clk_AC, ~counter_1_q[0], counter_1_q[1]);  // AND_Gate
  and and_4 (clk_RAM, counter_1_q[0], counter_1_q[1]);
  and JPZ (JPZ_out, \Instrução [7], \Instrução [6], ~\Instrução [5], ~\Instrução [4], clk_PC, Zero);  // AND_Gate
  nand nand_2 (nand_2_out, \Instrução [7], ~\Instrução [6], \Instrução [5]);  // NAND_Gate
  and and_5 (E, \Instrução [4], nand_2_out);

  assign D = \Instrução [4];
  assign Dados = \Instrução [3:0];
  assign \Endereçamento  = \Instrução [3:0];
  assign Operando = \Instrução [3:0];
  assign Rst_PC = Reset;
  assign S = \Instrução [7:5];
endmodule

module RGB (
  input  E,
  output E_2,
  output E_3
);

  wire clock_1_out, controlled_buffer_1_out, controlled_buffer_2_out, controlled_buffer_3_out;

  Clock clock_1 (.out(clock_1_out));
  assign controlled_buffer_1_out = E ? clock_1_out : 1'bz;  // Controlled_Buffer controlled_buffer_1
  assign controlled_buffer_2_out = controlled_buffer_1_out ? controlled_buffer_1_out : 1'bz;  // Controlled_Buffer controlled_buffer_2
  assign controlled_buffer_3_out = controlled_buffer_1_out ? controlled_buffer_1_out : 1'bz;  // Controlled_Buffer controlled_buffer_3
  and and_1 (E_2, controlled_buffer_2_out, controlled_buffer_3_out);
  assign E_3 = controlled_buffer_1_out ? 1'b0 : 1'bz;  // Controlled_Buffer controlled_buffer_4
endmodule
