// Logisim project Soma - 1.circ as structural Verilog: 2 circuits, main circuit Soma - 1
module Soma___1 (
  input  A,
  input  B,
  input  Vem_1,
  output Soma,
  output Vai_1
);

  wire and_1_out, and_2_out, or_1_out, xor_1_out;

  or or_1 (or_1_out, B, Vem_1);
  xor xor_1 (xor_1_out, A, B);
  xor xor_2 (Soma, xor_1_out, Vem_1);
  and and_1 (and_1_out, or_1_out, A);
  and and_2 (and_2_out, B, Vem_1);
  or or_2 (Vai_1, and_1_out, and_2_out);
endmodule

module Teste (
  input  A,
  input  B,
  input  vem_1,
  output vai_1,
  output Soma
);

  Soma___1 soma_1_1 (.A(A), .B(B), .Vem_1(vem_1), .Soma(Soma), .Vai_1(vai_1));
endmodule
