// Logisim project Soma - 4.circ as structural Verilog: 2 circuits, main circuit Soma - 4
module Soma___4 (
  input  [3:0] B,
  input  [3:0] A,
  output out_3,
  output [3:0] out_4
);

  wire soma_1_2_vai_1, soma_1_3_vai_1, soma_1_4_vai_1;

  Soma___1 soma_1_1 (.A(A[3]), .B(B[3]), .Vem_1(soma_1_2_vai_1), .Soma(out_4[3]), .Vai_1(out_3));
  Soma___1 soma_1_2 (.A(A[2]), .B(B[2]), .Vem_1(soma_1_3_vai_1), .Soma(out_4[2]), .Vai_1(soma_1_2_vai_1));
  Soma___1 soma_1_3 (.A(A[1]), .B(B[1]), .Vem_1(soma_1_4_vai_1), .Soma(out_4[1]), .Vai_1(soma_1_3_vai_1));
  Soma___1 soma_1_4 (.A(A[0]), .B(B[0]), .Vem_1(1'b0), .Soma(out_4[0]), .Vai_1(soma_1_4_vai_1));
endmodule

module Teste (
  input  [3:0] in_1,
  input  [3:0] in_2,
  output out_3,
  output [3:0] out_4
);

  // Soma___4 soma_4_1: pin names not known; wires that end beside it: out_3, in_1, in_2
endmodule
