// Logisim project Sub - 1.circ as structural Verilog: 4 circuits, main circuit Teste Sub - 1
module Teste_Sub___1 (
  input  B,
  input  A,
  input  in_3,
  output out_4,
  output out_5
);

  Sub___1 sub_1_1 (.A(A), .B(B), .Vem_1(out_4), .Sub(out_5), .Vai_1(in_3));
endmodule

module Sub___1 (
  input  A,
  input  B,
  input  Vem_1,
  output Sub,
  output Vai_1
);

  wire and_1_out, and_2_out, not_1_out, or_1_out, xor_1_out;

  not not_1 (not_1_out, A);
  or or_1 (or_1_out, B, Vem_1);
  xor xor_1 (xor_1_out, A, B);
  xor xor_2 (Sub, xor_1_out, Vem_1);
  and and_1 (and_1_out, or_1_out, not_1_out);
  and and_2 (and_2_out, B, Vem_1);
  or or_2 (Vai_1, and_1_out, and_2_out);
endmodule

module Sub___4 (
  input  [3:0] A,
  input  [3:0] in_2,
  output Vai_1,
  output [3:0] out_4
);

  wire sub_1_2_vai_1, sub_1_3_vai_1, sub_1_4_vai_1;

  Sub___1 sub_1_1 (.A(A[3]), .B(in_2[3]), .Vem_1(sub_1_2_vai_1), .Sub(out_4[3]), .Vai_1(Vai_1));
  Sub___1 sub_1_2 (.A(A[2]), .B(in_2[2]), .Vem_1(sub_1_3_vai_1), .Sub(out_4[2]), .Vai_1(sub_1_2_vai_1));
  Sub___1 sub_1_3 (.A(A[1]), .B(in_2[1]), .Vem_1(sub_1_4_vai_1), .Sub(out_4[1]), .Vai_1(sub_1_3_vai_1));
  Sub___1 sub_1_4 (.A(A[0]), .B(in_2[0]), .Vem_1(1'b0), .Sub(out_4[0]), .Vai_1(sub_1_4_vai_1));
endmodule

module Main (
  input  [3:0] A,
  input  [3:0] B,
  output out_3,
  output [3:0] Sub
);

  Sub___4 sub_4_1 (.A(A), .Vai_1(out_3), .in_2(B), .out_4(Sub));
endmodule
