// Logisim project Sub - 4.circ as structural Verilog: 2 circuits, main circuit Sub - 4
module Sub___4 (
  input  [3:0] A,
  input  [3:0] in_2,
  output Vai_1,
  output [3:0] out_4
);

  wire sub_1_2_vai_1, sub_1_3_vai_1, sub_1_4_vai_1;

  Sub___1 sub_1_1 (.A(A[3]), .B(in_2[3]), .Vem_1(sub_1_2_vai_1), .Sub(out_4[3]), .Vai_1(Vai_1));
  Sub___1 sub_1_2 (.A(A[2]), .B(in_2[2]), .Vem_1(sub_1_3_vai_1), .Sub(out_4[2]), .Vai_1(sub_1_2_vai_1));
  Sub___1 sub_1_3 (.A(A[1]), .B(in_2[1]), .Vem_1(sub_1_4_vai_1), .Sub(out_4[1]), .Vai_1(sub_1_3_vai_1));
  Sub___1 sub_1_4 (.A(A[0]), .B(in_2[0]), .Vem_1(1'b0), .Sub(out_4[0]), .Vai_1(sub_1_4_vai_1));
endmodule

module Teste (
  input  [3:0] A,
  input  [3:0] B,
  output Overflow,
  output [3:0] out_4
);

  Sub___4 sub_4_1 (.A(A), .Vai_1(Overflow), .in_2(B), .out_4(out_4));
endmodule
